// Logisim project EXP 2.circ as structural Verilog: 1 circuit, main circuit main
module main (
  input  [7:0] A,
  input  MOD_CONROL,
  input  [7:0] B,
  output out_4,
  output CALL,
  output [6:0] RESULT_A,
  output E,
  output [7:0] FINAL_A,
  output AVF
);

  wire comparator_1_eq, multiplexer_2_out, multiplexer_4_out, not_3_out;
  wire [6:0] adder_2_out, multiplexer_1_out, multiplexer_3_out, not_1_out, not_2_out;

  xor xor_1 (out_4, A[7], B[7]);
  assign not_1_out = ~B[6:0];  // NOT_Gate not_1, 7 bits wide
  Multiplexer #(.width(7), .enable("false")) multiplexer_1 (
    .in0(B[6:0]), .in1(not_1_out), .out(multiplexer_1_out), .sel(CALL));
  Comparator #(.width(7)) comparator_1 (.a(RESULT_A), .b({7{1'b0}}), .eq(comparator_1_eq));  // open: gt, lt
  xor xor_2 (CALL, out_4, MOD_CONROL);
  Adder #(.width(7)) adder_1 (.a(A[6:0]), .b(multiplexer_1_out), .out(RESULT_A), .cin(CALL), .cout(E));
  Multiplexer #(.enable("false")) multiplexer_2 (
    .in0(A[7]), .in1(1'b0), .out(multiplexer_2_out), .sel(comparator_1_eq));
  assign not_2_out = ~RESULT_A;  // NOT_Gate not_2, 7 bits wide
  not not_3 (not_3_out, A[7]);
  Adder #(.width(7)) adder_2 (.a(not_2_out), .b({7{1'b0}}), .out(adder_2_out), .cin(CALL));  // open: cout
  Multiplexer #(.width(7), .enable("false")) multiplexer_3 (
    .in0(adder_2_out), .in1(RESULT_A), .out(multiplexer_3_out), .sel(E));
  Multiplexer #(.enable("false")) multiplexer_4 (
    .in0(not_3_out), .in1(multiplexer_2_out), .out(multiplexer_4_out), .sel(E));
  Multiplexer #(.width(7), .enable("false")) multiplexer_5 (
    .in0(RESULT_A), .in1(multiplexer_3_out), .out(FINAL_A[6:0]), .sel(CALL));
  Multiplexer #(.enable("false")) multiplexer_6 (.in0(A[7]), .in1(multiplexer_4_out), .out(FINAL_A[7]), .sel(CALL));
  Multiplexer #(.enable("false")) multiplexer_7 (.in0(E), .in1(1'b0), .out(AVF), .sel(CALL));

  // Notes on the sheet:
  //   MOD=0 :ADDITION
  //   MOD=1 :SUBTRACTION
  //   sign=0 both have same sign
  //   sign=1 both have diff same sign
  //   23CS042
  //   CALL=0:FUNCTION 1
  //   CALL=1:FUNCTION 2
  //   FUNCTION:1 ADD TWO NUMBERS AND SIGN OF NUMBER A
  //   FUNCTION:2 SUBTRACT SMALLER NUMBER WITH LARGER AND THE SIGGN OF LARGER NUMBER
endmodule
