// Logisim project EXP_2.circ as structural Verilog
module ADD_SUB (
  input  M,
  input  [7:0] A,
  input  [7:0] B,
  output SIGN,
  output CALLING,
  output [6:0] RESULT_MAGNITUDE,
  output E,
  output AVF,
  output [7:0] FINAL_RESULT
);

  wire comparator_1_eq, multiplexer_2_out, multiplexer_3_out, not_3_out;
  wire [6:0] adder_2_out, multiplexer_1_out, multiplexer_4_out, not_1_out, not_2_out;

  Comparator #(.width(7)) comparator_1 (.a(RESULT_MAGNITUDE), .b({7{1'b0}}), .eq(comparator_1_eq));  // open: gt, lt
  Multiplexer #(.width(7), .enable("false")) multiplexer_1 (
    .in0(B[6:0]), .in1(not_1_out), .out(multiplexer_1_out), .sel(CALLING));
  assign not_1_out = ~B[6:0];  // NOT_Gate not_1, 7 bits wide
  assign not_2_out = ~RESULT_MAGNITUDE;  // NOT_Gate not_2, 7 bits wide
  not not_3 (not_3_out, A[7]);
  Multiplexer #(.enable("false")) multiplexer_2 (
    .in0(A[7]), .in1(1'b0), .out(multiplexer_2_out), .sel(comparator_1_eq));
  xor xor_1 (SIGN, A[7], B[7]);
  Adder #(.width(7)) adder_1 (.a(A[6:0]), .b(multiplexer_1_out), .out(RESULT_MAGNITUDE), .cin(CALLING), .cout(E));
  Adder #(.width(7)) adder_2 (.a(not_2_out), .b(7'b0000001), .out(adder_2_out));  // open: cin, cout
  Multiplexer #(.enable("false")) multiplexer_3 (
    .in0(not_3_out), .in1(multiplexer_2_out), .out(multiplexer_3_out), .sel(E));
  Multiplexer #(.width(7), .enable("false")) multiplexer_4 (
    .in0(adder_2_out), .in1(RESULT_MAGNITUDE), .out(multiplexer_4_out), .sel(E));
  xor xor_2 (CALLING, SIGN, M);
  Multiplexer #(.enable("false")) multiplexer_5 (.in0(E), .in1(1'b0), .out(AVF), .sel(CALLING));
  Multiplexer #(.width(7), .enable("false")) multiplexer_6 (
    .in0(RESULT_MAGNITUDE), .in1(multiplexer_4_out), .out(FINAL_RESULT[6:0]), .sel(M));
  Multiplexer #(.enable("false")) multiplexer_7 (.in0(A[7]), .in1(multiplexer_3_out), .out(FINAL_RESULT[7]), .sel(M));

  // Notes on the sheet:
  //   M=0 ADD
  //   M=1 SUB
  //   MAGNITUDE OF A HERE A=42
  //   MAGNITUDE OF B HERE B=55
  //   FUN1: ADD MAGNITUDE OF BOTH NUMS AND USE SIGN OF A
  //   S=1 BOTH ARE DIFFERENT SIGN
  //   FUN2: SUB SMALLER MAGNITUDE FROM LARGER MAGNITUSE AND USE SIGN OF LARGER NUM
  //   S=0 BOTH ARE SAME SIGN
  //   23CS042
  //   CALL=0 CALL FUN1
  //   CALL=1 CALL FUN2
endmodule
