// Logisim project EXP 3_POST_SESSION.circ as structural Verilog
module _5_bit_3_register (
  input  [1:0] SELECT_REGISTER,
  input  [4:0] Input_For_Register_C,
  input  [4:0] Input_For_Register_B,
  input  [4:0] Input_For_Register_A,
  input  CLEAR,
  output [4:0] out_6,
  output [4:0] O_P_FOR_C,
  output [4:0] O_P_FOR_B,
  output [4:0] O_P_FOR_A
);

  wire clock_1_out;

  Multiplexer #(.select(2), .enable("false")) multiplexer_1 (
    .in0(O_P_FOR_C[0]), .in1(O_P_FOR_B[0]), .in2(O_P_FOR_A[0]), .in3(O_P_FOR_A[0]), .out(out_6[0]),
    .sel(SELECT_REGISTER));
  Clock clock_1 (.out(clock_1_out));
  Register #(.width(5)) register_1 (.D(Input_For_Register_C), .en(1'b1), .Q(O_P_FOR_C), .clk(clock_1_out), .clr(CLEAR));
  Multiplexer #(.select(2), .enable("false")) multiplexer_2 (
    .in0(O_P_FOR_C[1]), .in1(O_P_FOR_B[1]), .in2(O_P_FOR_A[1]), .in3(O_P_FOR_A[1]), .out(out_6[1]),
    .sel(SELECT_REGISTER));
  Multiplexer #(.select(2), .enable("false")) multiplexer_3 (
    .in0(O_P_FOR_C[2]), .in1(O_P_FOR_B[2]), .in2(O_P_FOR_A[2]), .in3(O_P_FOR_A[2]), .out(out_6[2]),
    .sel(SELECT_REGISTER));
  Register #(.width(5)) register_2 (.D(Input_For_Register_B), .en(1'b1), .Q(O_P_FOR_B), .clk(clock_1_out), .clr(CLEAR));
  Multiplexer #(.select(2), .enable("false")) multiplexer_4 (
    .in0(O_P_FOR_C[3]), .in1(O_P_FOR_B[3]), .in2(O_P_FOR_A[3]), .in3(O_P_FOR_A[3]), .out(out_6[3]),
    .sel(SELECT_REGISTER));
  Multiplexer #(.select(2), .enable("false")) multiplexer_5 (
    .in0(O_P_FOR_C[4]), .in1(O_P_FOR_B[4]), .in2(O_P_FOR_A[4]), .in3(O_P_FOR_A[4]), .out(out_6[4]),
    .sel(SELECT_REGISTER));
  Register #(.width(5)) register_3 (.D(Input_For_Register_A), .en(1'b1), .Q(O_P_FOR_A), .clk(clock_1_out), .clr(CLEAR));

  // Notes on the sheet:
  //   M=(42%5)+3=5
  //   N=(42%3)+3=3
  //   00 => REGISTER C
  //   01 => REGISTER B
  //   10 => REGISTER A
  //   11 => REGISTER A
  //   BIT0
  //   BIT1
  //   23CS042
  //   BIT2
  //   BIT3
  //   BIT4
endmodule

module TRI_STATE_BUFFER (
  input  [1:0] SELECT_REGISTER,
  input  [4:0] Input_For_Register_C,
  input  [4:0] Input_For_Register_B,
  input  [4:0] Input_For_Register_A,
  input  CLEAR,
  output [4:0] out_6,
  output [4:0] O_P_FOR_C,
  output [4:0] O_P_FOR_B,
  output [4:0] O_P_FOR_A
);

  wire clock_1_out, decoder_1_out0, decoder_1_out1, decoder_1_out2;

  Decoder #(.select(2), .enable("false")) decoder_1 (
    .out0(decoder_1_out0), .out1(decoder_1_out1), .out2(decoder_1_out2), .out3(decoder_1_out2),
    .sel(SELECT_REGISTER));
  assign out_6[4] = decoder_1_out0 ? O_P_FOR_A[4] : 1'bz;  // Controlled_Buffer controlled_buffer_1
  Clock clock_1 (.out(clock_1_out));
  assign out_6[3] = decoder_1_out0 ? O_P_FOR_A[3] : 1'bz;  // Controlled_Buffer controlled_buffer_2
  assign out_6[4] = decoder_1_out1 ? O_P_FOR_B[4] : 1'bz;  // Controlled_Buffer controlled_buffer_3
  assign out_6[4] = decoder_1_out2 ? O_P_FOR_C[4] : 1'bz;  // Controlled_Buffer controlled_buffer_4
  assign out_6[2] = decoder_1_out0 ? O_P_FOR_A[2] : 1'bz;  // Controlled_Buffer controlled_buffer_5
  assign out_6[2] = decoder_1_out1 ? O_P_FOR_B[2] : 1'bz;  // Controlled_Buffer controlled_buffer_6
  assign out_6[3] = decoder_1_out1 ? O_P_FOR_B[3] : 1'bz;  // Controlled_Buffer controlled_buffer_7
  assign out_6[3] = decoder_1_out2 ? O_P_FOR_C[3] : 1'bz;  // Controlled_Buffer controlled_buffer_8
  Register #(.width(5)) register_1 (.D(Input_For_Register_C), .en(1'b1), .Q(O_P_FOR_C), .clk(clock_1_out), .clr(CLEAR));
  assign out_6[1] = decoder_1_out0 ? O_P_FOR_A[1] : 1'bz;  // Controlled_Buffer controlled_buffer_9
  assign out_6[0] = decoder_1_out0 ? O_P_FOR_A[0] : 1'bz;  // Controlled_Buffer controlled_buffer_10
  assign out_6[1] = decoder_1_out1 ? O_P_FOR_B[1] : 1'bz;  // Controlled_Buffer controlled_buffer_11
  assign out_6[2] = decoder_1_out2 ? O_P_FOR_C[2] : 1'bz;  // Controlled_Buffer controlled_buffer_12
  assign out_6[0] = decoder_1_out1 ? O_P_FOR_B[0] : 1'bz;  // Controlled_Buffer controlled_buffer_13
  assign out_6[1] = decoder_1_out2 ? O_P_FOR_C[1] : 1'bz;  // Controlled_Buffer controlled_buffer_14
  Register #(.width(5)) register_2 (.D(Input_For_Register_B), .en(1'b1), .Q(O_P_FOR_B), .clk(clock_1_out), .clr(CLEAR));
  assign out_6[0] = decoder_1_out2 ? O_P_FOR_C[0] : 1'bz;  // Controlled_Buffer controlled_buffer_15
  Register #(.width(5)) register_3 (.D(Input_For_Register_A), .en(1'b1), .Q(O_P_FOR_A), .clk(clock_1_out), .clr(CLEAR));

  // Notes on the sheet:
  //   M=(42%5)+3=5
  //   N=(42%3)+3=3
  //   00 => REGISTER A
  //   01 => REGISTER B
  //   10 => REGISTER C
  //   11 => REGISTER D
  //   A3
  //   A4
  //   B4
  //   B3
  //   C4
  //   C
  //   A2
  //   B2
  //   C3
  //   A1
  //   A0
  //   B1
  //   23CS042
  //   C2
  //   C1
  //   B0
  //   C0
  //   A
  //   B
endmodule
