// Logisim project EXP 4.circ as structural Verilog: 17 circuits, main circuit 1-BIT-ARITHMETIC
module _1_BIT_ARITHMETIC (
  input  Cin,
  input  B0,
  input  A0,
  input  [1:0] SELECT,
  output S0,
  output Cout
);

  wire multiplexer_1_out, not_1_out, not_2_out, xor_1_out;

  xor xor_1 (xor_1_out, B0, B0);
  not not_1 (not_1_out, B0);
  not not_2 (not_2_out, xor_1_out);
  Multiplexer #(.select(2), .enable("false")) multiplexer_1 (
    .in0(B0), .in1(not_1_out), .in2(xor_1_out), .in3(not_2_out), .out(multiplexer_1_out), .sel(SELECT));
  Adder #(.width(1)) adder_1 (.a(A0), .b(multiplexer_1_out), .out(S0), .cin(Cin), .cout(Cout));

  // Notes on the sheet:
  //   23CS042
endmodule

module _2_BIT_ARITHMETIC (
  input  [1:0] A,
  input  Cin,
  input  [1:0] B,
  input  [1:0] SELECT,
  output [1:0] S,
  output Cout
);

  wire adder_1_cout, multiplexer_1_out, multiplexer_2_out, not_1_out, not_2_out, not_3_out, not_4_out,
       xor_1_out, xor_2_out;

  not not_1 (not_1_out, B[0]);
  xor xor_1 (xor_1_out, B[0], B[0]);
  not not_2 (not_2_out, B[1]);
  xor xor_2 (xor_2_out, B[1], B[1]);
  Multiplexer #(.select(2), .enable("false")) multiplexer_1 (
    .in0(B[0]), .in1(not_1_out), .in2(xor_1_out), .in3(not_3_out), .out(multiplexer_1_out), .sel(SELECT));
  not not_3 (not_3_out, xor_1_out);
  Multiplexer #(.select(2), .enable("false")) multiplexer_2 (
    .in0(B[1]), .in1(not_2_out), .in2(xor_2_out), .in3(not_4_out), .out(multiplexer_2_out), .sel(SELECT));
  not not_4 (not_4_out, xor_2_out);
  Adder #(.width(1)) adder_1 (.a(A[0]), .b(multiplexer_1_out), .out(S[0]), .cin(Cin), .cout(adder_1_cout));
  Adder #(.width(1)) adder_2 (.a(A[1]), .b(multiplexer_2_out), .out(S[1]), .cin(adder_1_cout), .cout(Cout));

  // Notes on the sheet:
  //   23CS042
endmodule

module _4_BIT_ARITHMETIC (
  input  [3:0] A,
  input  Cin,
  input  [3:0] B,
  input  [1:0] SELECT,
  output [3:0] S,
  output Cout
);

  wire adder_1_cout, adder_2_cout, adder_3_cout, multiplexer_1_out, multiplexer_2_out, multiplexer_3_out,
       multiplexer_4_out, not_1_out, not_2_out, not_3_out, not_4_out, not_5_out, not_6_out, not_7_out,
       not_8_out, xor_1_out, xor_2_out, xor_3_out, xor_4_out;

  xor xor_1 (xor_1_out, B[0], B[0]);
  xor xor_2 (xor_2_out, B[1], B[1]);
  xor xor_3 (xor_3_out, B[2], B[2]);
  xor xor_4 (xor_4_out, B[3], B[3]);
  not not_1 (not_1_out, B[0]);
  not not_2 (not_2_out, xor_1_out);
  not not_3 (not_3_out, B[1]);
  not not_4 (not_4_out, xor_2_out);
  not not_5 (not_5_out, B[2]);
  not not_6 (not_6_out, xor_3_out);
  not not_7 (not_7_out, B[3]);
  not not_8 (not_8_out, xor_4_out);
  Multiplexer #(.select(2), .enable("false")) multiplexer_1 (
    .in0(B[0]), .in1(not_1_out), .in2(xor_1_out), .in3(not_2_out), .out(multiplexer_1_out), .sel(SELECT));
  Multiplexer #(.select(2), .enable("false")) multiplexer_2 (
    .in0(B[1]), .in1(not_3_out), .in2(xor_2_out), .in3(not_4_out), .out(multiplexer_2_out), .sel(SELECT));
  Multiplexer #(.select(2), .enable("false")) multiplexer_3 (
    .in0(B[2]), .in1(not_5_out), .in2(xor_3_out), .in3(not_6_out), .out(multiplexer_3_out), .sel(SELECT));
  Multiplexer #(.select(2), .enable("false")) multiplexer_4 (
    .in0(B[3]), .in1(not_7_out), .in2(xor_4_out), .in3(not_8_out), .out(multiplexer_4_out), .sel(SELECT));
  Adder #(.width(1)) adder_1 (.a(A[0]), .b(multiplexer_1_out), .out(S[0]), .cin(Cin), .cout(adder_1_cout));
  Adder #(.width(1)) adder_2 (.a(A[1]), .b(multiplexer_2_out), .out(S[1]), .cin(adder_1_cout), .cout(adder_2_cout));
  Adder #(.width(1)) adder_3 (.a(A[2]), .b(multiplexer_3_out), .out(S[2]), .cin(adder_2_cout), .cout(adder_3_cout));
  Adder #(.width(1)) adder_4 (.a(A[3]), .b(multiplexer_4_out), .out(S[3]), .cin(adder_3_cout), .cout(Cout));

  // Notes on the sheet:
  //   23CS042
endmodule

module _8_BIT_ARITHMETIC (
  input  [7:0] A,
  input  Cin,
  input  [7:0] B,
  input  [1:0] SELECT,
  output [7:0] S,
  output Cout
);

  wire adder_1_cout, adder_2_cout, adder_3_cout, adder_4_cout, adder_5_cout, adder_6_cout, adder_7_cout,
       multiplexer_1_out, multiplexer_2_out, multiplexer_3_out, multiplexer_4_out, multiplexer_5_out,
       multiplexer_6_out, multiplexer_7_out, multiplexer_8_out, not_1_out, not_2_out, not_3_out, not_4_out,
       not_5_out, not_6_out, not_7_out, not_8_out, not_9_out, not_10_out, not_11_out, not_12_out, not_13_out,
       not_14_out, not_15_out, not_16_out, xor_1_out, xor_2_out, xor_3_out, xor_4_out, xor_5_out, xor_6_out,
       xor_7_out, xor_8_out;

  not not_1 (not_1_out, B[0]);
  xor xor_1 (xor_1_out, B[0], B[0]);
  not not_2 (not_2_out, B[1]);
  xor xor_2 (xor_2_out, B[1], B[1]);
  not not_3 (not_3_out, B[2]);
  xor xor_3 (xor_3_out, B[2], B[2]);
  not not_4 (not_4_out, B[3]);
  xor xor_4 (xor_4_out, B[3], B[3]);
  not not_5 (not_5_out, B[4]);
  xor xor_5 (xor_5_out, B[4], B[4]);
  not not_6 (not_6_out, B[5]);
  xor xor_6 (xor_6_out, B[5], B[5]);
  not not_7 (not_7_out, B[6]);
  xor xor_7 (xor_7_out, B[6], B[6]);
  not not_8 (not_8_out, B[7]);
  xor xor_8 (xor_8_out, B[7], B[7]);
  Multiplexer #(.select(2), .enable("false")) multiplexer_1 (
    .in0(B[0]), .in1(not_1_out), .in2(xor_1_out), .in3(not_9_out), .out(multiplexer_1_out), .sel(SELECT));
  not not_9 (not_9_out, xor_1_out);
  Multiplexer #(.select(2), .enable("false")) multiplexer_2 (
    .in0(B[1]), .in1(not_2_out), .in2(xor_2_out), .in3(not_10_out), .out(multiplexer_2_out), .sel(SELECT));
  not not_10 (not_10_out, xor_2_out);
  Multiplexer #(.select(2), .enable("false")) multiplexer_3 (
    .in0(B[2]), .in1(not_3_out), .in2(xor_3_out), .in3(not_11_out), .out(multiplexer_3_out), .sel(SELECT));
  not not_11 (not_11_out, xor_3_out);
  Multiplexer #(.select(2), .enable("false")) multiplexer_4 (
    .in0(B[3]), .in1(not_4_out), .in2(xor_4_out), .in3(not_12_out), .out(multiplexer_4_out), .sel(SELECT));
  not not_12 (not_12_out, xor_4_out);
  Multiplexer #(.select(2), .enable("false")) multiplexer_5 (
    .in0(B[4]), .in1(not_5_out), .in2(xor_5_out), .in3(not_13_out), .out(multiplexer_5_out), .sel(SELECT));
  not not_13 (not_13_out, xor_5_out);
  Multiplexer #(.select(2), .enable("false")) multiplexer_6 (
    .in0(B[5]), .in1(not_6_out), .in2(xor_6_out), .in3(not_14_out), .out(multiplexer_6_out), .sel(SELECT));
  not not_14 (not_14_out, xor_6_out);
  Multiplexer #(.select(2), .enable("false")) multiplexer_7 (
    .in0(B[6]), .in1(not_7_out), .in2(xor_7_out), .in3(not_15_out), .out(multiplexer_7_out), .sel(SELECT));
  not not_15 (not_15_out, xor_7_out);
  Multiplexer #(.select(2), .enable("false")) multiplexer_8 (
    .in0(B[7]), .in1(not_8_out), .in2(xor_8_out), .in3(not_16_out), .out(multiplexer_8_out), .sel(SELECT));
  not not_16 (not_16_out, xor_8_out);
  Adder #(.width(1)) adder_1 (.a(A[0]), .b(multiplexer_1_out), .out(S[0]), .cin(Cin), .cout(adder_1_cout));
  Adder #(.width(1)) adder_2 (.a(A[1]), .b(multiplexer_2_out), .out(S[1]), .cin(adder_1_cout), .cout(adder_2_cout));
  Adder #(.width(1)) adder_3 (.a(A[2]), .b(multiplexer_3_out), .out(S[2]), .cin(adder_2_cout), .cout(adder_3_cout));
  Adder #(.width(1)) adder_4 (.a(A[3]), .b(multiplexer_4_out), .out(S[3]), .cin(adder_3_cout), .cout(adder_4_cout));
  Adder #(.width(1)) adder_5 (.a(A[4]), .b(multiplexer_5_out), .out(S[4]), .cin(adder_4_cout), .cout(adder_5_cout));
  Adder #(.width(1)) adder_6 (.a(A[5]), .b(multiplexer_6_out), .out(S[5]), .cin(adder_5_cout), .cout(adder_6_cout));
  Adder #(.width(1)) adder_7 (.a(A[6]), .b(multiplexer_7_out), .out(S[6]), .cin(adder_6_cout), .cout(adder_7_cout));
  Adder #(.width(1)) adder_8 (.a(A[7]), .b(multiplexer_8_out), .out(S[7]), .cin(adder_7_cout), .cout(Cout));

  // Notes on the sheet:
  //   23CS042
  //   23CS042
endmodule

module _1_BIT_LOGICAL (
  input  A0,
  input  B0,
  input  [1:0] SELECT,
  output OUTPUT
);

  wire and_1_out, not_1_out, or_1_out, xor_1_out;

  and and_1 (and_1_out, A0, B0);
  or or_1 (or_1_out, B0, A0);
  xor xor_1 (xor_1_out, B0, A0);
  not not_1 (not_1_out, A0);
  Multiplexer #(.select(2), .enable("false")) multiplexer_1 (
    .in0(and_1_out), .in1(or_1_out), .in2(xor_1_out), .in3(not_1_out), .out(OUTPUT), .sel(SELECT));

  // Notes on the sheet:
  //   23CS042
endmodule

module _2_BIT_LOGICAL (
  input  [1:0] A,
  input  [1:0] B,
  input  [1:0] SELECT,
  output [1:0] OUTPUT
);

  wire and_1_out, and_2_out, not_1_out, not_2_out, or_1_out, or_2_out, xor_1_out, xor_2_out;

  and and_1 (and_1_out, A[0], B[0]);
  or or_1 (or_1_out, B[0], A[0]);
  xor xor_1 (xor_1_out, B[0], A[0]);
  not not_1 (not_1_out, A[0]);
  and and_2 (and_2_out, A[1], B[1]);
  or or_2 (or_2_out, B[1], A[1]);
  xor xor_2 (xor_2_out, B[1], A[1]);
  not not_2 (not_2_out, A[1]);
  Multiplexer #(.select(2), .enable("false")) multiplexer_1 (
    .in0(and_1_out), .in1(or_1_out), .in2(xor_1_out), .in3(not_1_out), .out(OUTPUT[0]), .sel(SELECT));
  Multiplexer #(.select(2), .enable("false")) multiplexer_2 (
    .in0(and_2_out), .in1(or_2_out), .in2(xor_2_out), .in3(not_2_out), .out(OUTPUT[1]), .sel(SELECT));

  // Notes on the sheet:
  //   23CS042
endmodule

module _4_BIT_LOGICAL (
  input  [3:0] A,
  input  [3:0] B,
  input  [1:0] SELECT,
  output [3:0] OUTPUT
);

  wire and_1_out, and_2_out, and_3_out, and_4_out, not_1_out, not_2_out, not_3_out, not_4_out, or_1_out,
       or_2_out, or_3_out, or_4_out, xor_1_out, xor_2_out, xor_3_out, xor_4_out;

  and and_1 (and_1_out, A[0], B[0]);
  or or_1 (or_1_out, B[0], A[0]);
  not not_1 (not_1_out, A[0]);
  and and_2 (and_2_out, A[1], B[1]);
  or or_2 (or_2_out, B[1], A[1]);
  not not_2 (not_2_out, A[1]);
  xor xor_1 (xor_1_out, B[0], A[0]);
  xor xor_2 (xor_2_out, B[1], A[1]);
  and and_3 (and_3_out, A[2], B[2]);
  or or_3 (or_3_out, B[2], A[2]);
  xor xor_3 (xor_3_out, B[2], A[2]);
  not not_3 (not_3_out, A[2]);
  and and_4 (and_4_out, A[3], B[3]);
  or or_4 (or_4_out, B[3], A[3]);
  xor xor_4 (xor_4_out, B[3], A[3]);
  not not_4 (not_4_out, A[3]);
  Multiplexer #(.select(2), .enable("false")) multiplexer_1 (
    .in0(and_1_out), .in1(or_1_out), .in2(xor_1_out), .in3(not_1_out), .out(OUTPUT[0]), .sel(SELECT));
  Multiplexer #(.select(2), .enable("false")) multiplexer_2 (
    .in0(and_2_out), .in1(or_2_out), .in2(xor_2_out), .in3(not_2_out), .out(OUTPUT[1]), .sel(SELECT));
  Multiplexer #(.select(2), .enable("false")) multiplexer_3 (
    .in0(and_3_out), .in1(or_3_out), .in2(xor_3_out), .in3(not_3_out), .out(OUTPUT[2]), .sel(SELECT));
  Multiplexer #(.select(2), .enable("false")) multiplexer_4 (
    .in0(and_4_out), .in1(or_4_out), .in2(xor_4_out), .in3(not_4_out), .out(OUTPUT[3]), .sel(SELECT));

  // Notes on the sheet:
  //   23CS042
endmodule

module _8_BIT_LOGICAL (
  input  [7:0] A,
  input  [7:0] B,
  input  [1:0] SELECT,
  output [7:0] OUTPUT
);

  wire and_1_out, and_2_out, and_3_out, and_4_out, and_5_out, and_6_out, and_7_out, and_8_out, not_1_out,
       not_2_out, not_3_out, not_4_out, not_5_out, not_6_out, not_7_out, not_8_out, or_1_out, or_2_out,
       or_3_out, or_4_out, or_5_out, or_6_out, or_7_out, or_8_out, xor_1_out, xor_2_out, xor_3_out,
       xor_4_out, xor_5_out, xor_6_out, xor_7_out, xor_8_out;

  and and_1 (and_1_out, A[0], B[0]);
  or or_1 (or_1_out, B[0], A[0]);
  xor xor_1 (xor_1_out, B[0], A[0]);
  not not_1 (not_1_out, A[0]);
  and and_2 (and_2_out, A[1], B[1]);
  or or_2 (or_2_out, B[1], A[1]);
  xor xor_2 (xor_2_out, B[1], A[1]);
  not not_2 (not_2_out, A[1]);
  and and_3 (and_3_out, A[2], B[2]);
  or or_3 (or_3_out, B[2], A[2]);
  not not_3 (not_3_out, A[2]);
  and and_4 (and_4_out, A[3], B[3]);
  or or_4 (or_4_out, B[3], A[3]);
  not not_4 (not_4_out, A[3]);
  and and_5 (and_5_out, A[4], B[4]);
  or or_5 (or_5_out, B[4], A[4]);
  xor xor_3 (xor_3_out, B[4], A[4]);
  not not_5 (not_5_out, A[4]);
  and and_6 (and_6_out, A[5], B[5]);
  or or_6 (or_6_out, B[5], A[5]);
  xor xor_4 (xor_4_out, B[5], A[5]);
  not not_6 (not_6_out, A[5]);
  and and_7 (and_7_out, A[6], B[6]);
  or or_7 (or_7_out, B[6], A[6]);
  not not_7 (not_7_out, A[6]);
  and and_8 (and_8_out, A[7], B[7]);
  or or_8 (or_8_out, B[7], A[7]);
  not not_8 (not_8_out, A[7]);
  xor xor_5 (xor_5_out, B[2], A[2]);
  xor xor_6 (xor_6_out, B[3], A[3]);
  xor xor_7 (xor_7_out, B[6], A[6]);
  xor xor_8 (xor_8_out, B[7], A[7]);
  Multiplexer #(.select(2), .enable("false")) multiplexer_1 (
    .in0(and_1_out), .in1(or_1_out), .in2(xor_1_out), .in3(not_1_out), .out(OUTPUT[0]), .sel(SELECT));
  Multiplexer #(.select(2), .enable("false")) multiplexer_2 (
    .in0(and_2_out), .in1(or_2_out), .in2(xor_2_out), .in3(not_2_out), .out(OUTPUT[1]), .sel(SELECT));
  Multiplexer #(.select(2), .enable("false")) multiplexer_3 (
    .in0(and_3_out), .in1(or_3_out), .in2(xor_5_out), .in3(not_3_out), .out(OUTPUT[2]), .sel(SELECT));
  Multiplexer #(.select(2), .enable("false")) multiplexer_4 (
    .in0(and_4_out), .in1(or_4_out), .in2(xor_6_out), .in3(not_4_out), .out(OUTPUT[3]), .sel(SELECT));
  Multiplexer #(.select(2), .enable("false")) multiplexer_5 (
    .in0(and_5_out), .in1(or_5_out), .in2(xor_3_out), .in3(not_5_out), .out(OUTPUT[4]), .sel(SELECT));
  Multiplexer #(.select(2), .enable("false")) multiplexer_6 (
    .in0(and_6_out), .in1(or_6_out), .in2(xor_4_out), .in3(not_6_out), .out(OUTPUT[5]), .sel(SELECT));
  Multiplexer #(.select(2), .enable("false")) multiplexer_7 (
    .in0(and_7_out), .in1(or_7_out), .in2(xor_7_out), .in3(not_7_out), .out(OUTPUT[6]), .sel(SELECT));
  Multiplexer #(.select(2), .enable("false")) multiplexer_8 (
    .in0(and_8_out), .in1(or_8_out), .in2(xor_8_out), .in3(not_8_out), .out(OUTPUT[7]), .sel(SELECT));

  // Notes on the sheet:
  //   23CS042
  //   23CS042
endmodule

module _1_BIT_16_LOGICAL (
  input  A,
  input  B,
  input  [3:0] SELECT,
  output OUTPUT
);

  wire and_1_out, and_2_out, and_3_out, not_1_out, not_2_out, not_3_out, not_4_out, not_5_out, or_1_out,
       or_2_out, or_3_out, xor_1_out;

  not not_1 (not_1_out, A);
  not not_2 (not_2_out, B);
  and and_1 (and_1_out, A, B);
  and and_2 (and_2_out, A, not_2_out);
  and and_3 (and_3_out, not_1_out, B);
  xor xor_1 (xor_1_out, A, B);
  or or_1 (or_1_out, A, B);
  or or_2 (or_2_out, A, not_2_out);
  or or_3 (or_3_out, not_1_out, B);
  not not_3 (not_3_out, or_1_out);
  not not_4 (not_4_out, xor_1_out);
  Multiplexer #(.select(4), .enable("false")) multiplexer_1 (
    .in0(1'b0), .in1(and_1_out), .in2(and_2_out), .in3(A), .in4(and_3_out), .in5(B), .in6(xor_1_out),
    .in7(or_1_out), .in8(not_3_out), .in9(not_4_out), .in10(not_2_out), .in11(or_2_out), .in12(not_1_out),
    .in13(or_3_out), .in14(not_5_out), .in15(1'b1), .out(OUTPUT), .sel(SELECT));
  not not_5 (not_5_out, and_1_out);

  // Notes on the sheet:
  //   23CS042
endmodule

module _2_BIT_16_LOGICAL (
  input  [1:0] A,
  input  [1:0] B,
  input  [3:0] SELECT,
  output [1:0] OUTPUT
);

  wire and_1_out, and_2_out, and_3_out, and_4_out, and_5_out, and_6_out, not_1_out, not_2_out, not_3_out,
       not_4_out, not_5_out, not_6_out, not_7_out, not_8_out, not_9_out, not_10_out, or_1_out, or_2_out,
       or_3_out, or_4_out, or_5_out, or_6_out, xor_1_out, xor_2_out;

  not not_1 (not_1_out, A[0]);
  not not_2 (not_2_out, B[0]);
  not not_3 (not_3_out, A[1]);
  not not_4 (not_4_out, B[1]);
  and and_1 (and_1_out, A[0], B[0]);
  and and_2 (and_2_out, A[0], not_2_out);
  and and_3 (and_3_out, not_1_out, B[0]);
  xor xor_1 (xor_1_out, A[0], B[0]);
  or or_1 (or_1_out, A[0], B[0]);
  or or_2 (or_2_out, A[0], not_2_out);
  or or_3 (or_3_out, not_1_out, B[0]);
  and and_4 (and_4_out, A[1], B[1]);
  and and_5 (and_5_out, A[1], not_4_out);
  and and_6 (and_6_out, not_3_out, B[1]);
  xor xor_2 (xor_2_out, A[1], B[1]);
  or or_4 (or_4_out, A[1], B[1]);
  or or_5 (or_5_out, A[1], not_4_out);
  or or_6 (or_6_out, not_3_out, B[1]);
  not not_5 (not_5_out, or_1_out);
  not not_6 (not_6_out, xor_1_out);
  not not_7 (not_7_out, or_4_out);
  not not_8 (not_8_out, xor_2_out);
  not not_9 (not_9_out, and_1_out);
  not not_10 (not_10_out, and_4_out);
  Multiplexer #(.select(4), .enable("false")) multiplexer_1 (
    .in0(1'b0), .in1(and_1_out), .in2(and_2_out), .in3(A[0]), .in4(and_3_out), .in5(B[0]), .in6(xor_1_out),
    .in7(or_1_out), .in8(not_5_out), .in9(not_6_out), .in10(not_2_out), .in11(or_2_out), .in12(not_1_out),
    .in13(or_3_out), .in14(not_9_out), .in15(1'b1), .out(OUTPUT[0]), .sel(SELECT));
  Multiplexer #(.select(4), .enable("false")) multiplexer_2 (
    .in0(1'b0), .in1(and_4_out), .in2(and_5_out), .in3(A[1]), .in4(and_6_out), .in5(B[1]), .in6(xor_2_out),
    .in7(or_4_out), .in8(not_7_out), .in9(not_8_out), .in10(not_4_out), .in11(or_5_out), .in12(not_3_out),
    .in13(or_6_out), .in14(not_10_out), .in15(1'b1), .out(OUTPUT[1]), .sel(SELECT));

  // Notes on the sheet:
  //   23CS042
endmodule

module _2_BIT_BIDIRECTIONAL (
  input  [1:0] I_P,
  input  I_P_BIT,
  input  CONTROL,
  output [1:0] O_P
);

  wire demultiplexer_1_out0, demultiplexer_1_out1, not_1_out;

  Demultiplexer #(.enable("false")) demultiplexer_1 (
    .out0(demultiplexer_1_out0), .out1(demultiplexer_1_out1), .in(I_P_BIT), .sel(not_1_out));
  not not_1 (not_1_out, CONTROL);
  Multiplexer #(.enable("false")) multiplexer_1 (.in0(demultiplexer_1_out1), .in1(I_P[0]), .out(O_P[1]), .sel(CONTROL));
  Multiplexer #(.enable("false")) multiplexer_2 (.in0(I_P[1]), .in1(demultiplexer_1_out0), .out(O_P[0]), .sel(CONTROL));

  // Notes on the sheet:
  //   0=> RIGHT SHEFT
  //   1=> LEFT SHEFT
  //   23CS042
endmodule

module _4_BIT_BIDIRECTIONAL (
  input  [3:0] I_P,
  input  I_P_2,
  input  CONTROL,
  output [3:0] O_P
);

  wire demultiplexer_1_out0, demultiplexer_1_out1, not_1_out;

  Demultiplexer #(.enable("false")) demultiplexer_1 (
    .out0(demultiplexer_1_out0), .out1(demultiplexer_1_out1), .in(I_P_2), .sel(not_1_out));
  not not_1 (not_1_out, CONTROL);
  Multiplexer #(.enable("false")) multiplexer_1 (.in0(demultiplexer_1_out1), .in1(I_P[2]), .out(O_P[3]), .sel(CONTROL));
  Multiplexer #(.enable("false")) multiplexer_2 (.in0(I_P[3]), .in1(I_P[1]), .out(O_P[2]), .sel(CONTROL));
  Multiplexer #(.enable("false")) multiplexer_3 (.in0(I_P[2]), .in1(I_P[0]), .out(O_P[1]), .sel(CONTROL));
  Multiplexer #(.enable("false")) multiplexer_4 (.in0(I_P[1]), .in1(demultiplexer_1_out0), .out(O_P[0]), .sel(CONTROL));

  // Notes on the sheet:
  //   0=> RIGHT SHEFT
  //   1=> LEFT SHEFT
  //   23CS042
endmodule

module _1_BIT_ALU (
  input  Cin,
  input  A0,
  input  B0,
  input  [1:0] SELECT_OPRATIONS,
  input  SHR,
  input  SHL,
  input  [1:0] ALU_SELECT_OPRATION,
  output Cout,
  output S
);

  wire n1_bit_arithmetic_1_s0, n1_bit_logical_1_output;

  _1_BIT_ARITHMETIC u_1_bit_arithmetic_1 (
    .Cin(Cin), .B0(B0), .A0(A0), .SELECT(SELECT_OPRATIONS), .S0(n1_bit_arithmetic_1_s0), .Cout(Cout));
  _1_BIT_LOGICAL u_1_bit_logical_1 (.A0(A0), .B0(B0), .SELECT(SELECT_OPRATIONS), .OUTPUT(n1_bit_logical_1_output));
  Multiplexer #(.select(2), .enable("false")) multiplexer_1 (
    .in0(n1_bit_arithmetic_1_s0), .in1(n1_bit_logical_1_output), .in2(SHR), .in3(SHL), .out(S),
    .sel(ALU_SELECT_OPRATION));

  // Notes on the sheet:
  //   00=> ARITHMETIC OPRATION
  //   01=>LOGICAL OPRATION
  //   10=> SHIFT RIGHT
  //   11=> SHIFT LEFT
  //   23CS042
endmodule

module _8_BIT_BIDIRECTIONAL (
  input  [7:0] I_P,
  input  I_P_2,
  input  CONTROL,
  output [7:0] O_P
);

  wire demultiplexer_1_out0, demultiplexer_1_out1, not_1_out;

  Demultiplexer #(.enable("false")) demultiplexer_1 (
    .out0(demultiplexer_1_out0), .out1(demultiplexer_1_out1), .in(I_P_2), .sel(not_1_out));
  not not_1 (not_1_out, CONTROL);
  Multiplexer #(.enable("false")) multiplexer_1 (.in0(demultiplexer_1_out1), .in1(I_P[6]), .out(O_P[7]), .sel(CONTROL));
  Multiplexer #(.enable("false")) multiplexer_2 (.in0(I_P[7]), .in1(I_P[5]), .out(O_P[6]), .sel(CONTROL));
  Multiplexer #(.enable("false")) multiplexer_3 (.in0(I_P[6]), .in1(I_P[4]), .out(O_P[5]), .sel(CONTROL));
  Multiplexer #(.enable("false")) multiplexer_4 (.in0(I_P[5]), .in1(I_P[3]), .out(O_P[4]), .sel(CONTROL));
  Multiplexer #(.enable("false")) multiplexer_5 (.in0(I_P[4]), .in1(I_P[2]), .out(O_P[3]), .sel(CONTROL));
  Multiplexer #(.enable("false")) multiplexer_6 (.in0(I_P[3]), .in1(I_P[1]), .out(O_P[2]), .sel(CONTROL));
  Multiplexer #(.enable("false")) multiplexer_7 (.in0(I_P[2]), .in1(I_P[0]), .out(O_P[1]), .sel(CONTROL));
  Multiplexer #(.enable("false")) multiplexer_8 (.in0(I_P[1]), .in1(demultiplexer_1_out0), .out(O_P[0]), .sel(CONTROL));

  // Notes on the sheet:
  //   0=> RIGHT SHEFT
  //   1=> LEFT SHEFT
  //   23CS042
endmodule

module _2_BIT_ALU (
  input  [1:0] B,
  input  Cin,
  input  [1:0] A,
  input  [1:0] SELECT_OPRATIONS,
  input  I_P_BIT,
  input  CONTROL,
  input  [1:0] ALU_SELECT_OPRATION,
  output Cout,
  output [1:0] S
);

  wire n1_bit_arithmetic_1_cout;
  wire [1:0] demultiplexer_1_out0, demultiplexer_1_out1, n1_bit_arithmetic_1_s0, n1_bit_logical_1_output,
       n2_bit_bidirectional_1_o_p;

  _1_BIT_ARITHMETIC u_1_bit_arithmetic_1 (
    .Cin(Cin), .B0(B[0]), .A0(A[0]), .SELECT(SELECT_OPRATIONS), .S0(n1_bit_arithmetic_1_s0[0]),
    .Cout(n1_bit_arithmetic_1_cout));
  _1_BIT_LOGICAL u_1_bit_logical_1 (
    .A0(A[0]), .B0(B[0]), .SELECT(SELECT_OPRATIONS), .OUTPUT(n1_bit_logical_1_output[0]));
  _2_BIT_BIDIRECTIONAL u_2_bit_bidirectional_1 (
    .I_P(A), .I_P_BIT(I_P_BIT), .CONTROL(CONTROL), .O_P(n2_bit_bidirectional_1_o_p));
  _1_BIT_ARITHMETIC u_1_bit_arithmetic_2 (
    .Cin(n1_bit_arithmetic_1_cout), .B0(B[1]), .A0(A[1]), .SELECT(SELECT_OPRATIONS),
    .S0(n1_bit_arithmetic_1_s0[1]), .Cout(Cout));
  _1_BIT_LOGICAL u_1_bit_logical_2 (
    .A0(A[1]), .B0(B[1]), .SELECT(SELECT_OPRATIONS), .OUTPUT(n1_bit_logical_1_output[1]));
  Demultiplexer #(.width(2), .enable("false")) demultiplexer_1 (
    .out0(demultiplexer_1_out0), .out1(demultiplexer_1_out1), .in(n2_bit_bidirectional_1_o_p), .sel(CONTROL));
  Multiplexer #(.select(2), .width(2), .enable("false")) multiplexer_1 (
    .in0(n1_bit_arithmetic_1_s0), .in1(n1_bit_logical_1_output), .in2(demultiplexer_1_out0),
    .in3(demultiplexer_1_out1), .out(S), .sel(ALU_SELECT_OPRATION));

  // Notes on the sheet:
  //   0=> RIGHT SHEFT
  //   1=> LEFT SHEFT
  //   23CS042
endmodule

module _4_BIT_ALU (
  input  [3:0] B,
  input  Cin,
  input  [3:0] A,
  input  [1:0] ALU_SELECT_OPRATION,
  input  [1:0] SELECT_OPRATIONS,
  output [3:0] S,
  output Cout
);

  wire n1_bit_arithmetic_1_cout, n1_bit_arithmetic_2_cout, n1_bit_arithmetic_3_cout;
  wire [3:0] n1_bit_arithmetic_1_s0, n1_bit_logical_1_output, undriven, undriven_2;

  _1_BIT_ARITHMETIC u_1_bit_arithmetic_1 (
    .Cin(Cin), .B0(B[2]), .A0(A[2]), .SELECT(SELECT_OPRATIONS), .S0(n1_bit_arithmetic_1_s0[0]),
    .Cout(n1_bit_arithmetic_1_cout));
  _1_BIT_LOGICAL u_1_bit_logical_1 (
    .A0(A[2]), .B0(B[2]), .SELECT(SELECT_OPRATIONS), .OUTPUT(n1_bit_logical_1_output[0]));
  _1_BIT_ARITHMETIC u_1_bit_arithmetic_2 (
    .Cin(n1_bit_arithmetic_1_cout), .B0(B[3]), .A0(A[3]), .SELECT(SELECT_OPRATIONS),
    .S0(n1_bit_arithmetic_1_s0[1]), .Cout(n1_bit_arithmetic_2_cout));
  _1_BIT_LOGICAL u_1_bit_logical_2 (
    .A0(A[3]), .B0(B[3]), .SELECT(SELECT_OPRATIONS), .OUTPUT(n1_bit_logical_1_output[1]));
  _1_BIT_ARITHMETIC u_1_bit_arithmetic_3 (
    .Cin(n1_bit_arithmetic_2_cout), .B0(B[1]), .A0(A[1]), .SELECT(SELECT_OPRATIONS),
    .S0(n1_bit_arithmetic_1_s0[2]), .Cout(n1_bit_arithmetic_3_cout));
  _1_BIT_LOGICAL u_1_bit_logical_3 (
    .A0(A[1]), .B0(B[1]), .SELECT(SELECT_OPRATIONS), .OUTPUT(n1_bit_logical_1_output[2]));
  _1_BIT_ARITHMETIC u_1_bit_arithmetic_4 (
    .Cin(n1_bit_arithmetic_3_cout), .B0(B[0]), .A0(A[0]), .SELECT(SELECT_OPRATIONS),
    .S0(n1_bit_arithmetic_1_s0[3]), .Cout(Cout));
  _1_BIT_LOGICAL u_1_bit_logical_4 (
    .A0(A[0]), .B0(B[0]), .SELECT(SELECT_OPRATIONS), .OUTPUT(n1_bit_logical_1_output[3]));
  Multiplexer #(.select(2), .width(4), .enable("false")) multiplexer_1 (
    .in0(n1_bit_arithmetic_1_s0), .in1(n1_bit_logical_1_output), .in2(undriven), .in3(undriven_2), .out(S),
    .sel(ALU_SELECT_OPRATION));

  // Notes on the sheet:
  //   23CS042
endmodule

module _8_BIT_ALU (
  input  [7:0] B,
  input  Cin,
  input  [7:0] A,
  input  [7:0] I_P,
  input  I_P_BIT,
  input  CONTROL,
  input  [1:0] ALU_SELECT_OPRATION,
  input  [1:0] SELECT_OPRATIONS,
  input  I_P_BIT_2,
  input  CONTROL_2,
  output Cout
);

  wire n1_bit_arithmetic_1_cout, n1_bit_arithmetic_2_cout, n1_bit_arithmetic_3_cout,
       n1_bit_arithmetic_4_cout, n1_bit_arithmetic_5_cout, n1_bit_arithmetic_6_cout, n1_bit_arithmetic_7_cout;
  wire [1:0] demultiplexer_1_out0, demultiplexer_1_out1, demultiplexer_2_out0, demultiplexer_2_out1,
       demultiplexer_3_out0, demultiplexer_3_out1, demultiplexer_4_out0, demultiplexer_4_out1,
       n2_bit_bidirectional_1_o_p, n2_bit_bidirectional_2_o_p, n2_bit_bidirectional_3_o_p,
       n2_bit_bidirectional_4_o_p;
  wire [3:0] n1_bit_arithmetic_1_s0, n1_bit_arithmetic_5_s0, n1_bit_logical_1_output, n1_bit_logical_5_output;

  _1_BIT_ARITHMETIC u_1_bit_arithmetic_1 (
    .Cin(Cin), .B0(B[6]), .A0(A[6]), .SELECT(SELECT_OPRATIONS), .S0(n1_bit_arithmetic_1_s0[0]),
    .Cout(n1_bit_arithmetic_1_cout));
  _1_BIT_LOGICAL u_1_bit_logical_1 (
    .A0(A[6]), .B0(B[6]), .SELECT(SELECT_OPRATIONS), .OUTPUT(n1_bit_logical_1_output[0]));
  _1_BIT_ARITHMETIC u_1_bit_arithmetic_2 (
    .Cin(n1_bit_arithmetic_1_cout), .B0(B[7]), .A0(A[7]), .SELECT(SELECT_OPRATIONS),
    .S0(n1_bit_arithmetic_1_s0[1]), .Cout(n1_bit_arithmetic_2_cout));
  _1_BIT_LOGICAL u_1_bit_logical_2 (
    .A0(A[7]), .B0(B[7]), .SELECT(SELECT_OPRATIONS), .OUTPUT(n1_bit_logical_1_output[1]));
  _1_BIT_ARITHMETIC u_1_bit_arithmetic_3 (
    .Cin(n1_bit_arithmetic_2_cout), .B0(B[5]), .A0(A[5]), .SELECT(SELECT_OPRATIONS),
    .S0(n1_bit_arithmetic_1_s0[2]), .Cout(n1_bit_arithmetic_3_cout));
  _1_BIT_LOGICAL u_1_bit_logical_3 (
    .A0(A[5]), .B0(B[5]), .SELECT(SELECT_OPRATIONS), .OUTPUT(n1_bit_logical_1_output[2]));
  _1_BIT_ARITHMETIC u_1_bit_arithmetic_4 (
    .Cin(n1_bit_arithmetic_3_cout), .B0(B[4]), .A0(A[4]), .SELECT(SELECT_OPRATIONS),
    .S0(n1_bit_arithmetic_1_s0[3]), .Cout(n1_bit_arithmetic_4_cout));
  _1_BIT_LOGICAL u_1_bit_logical_4 (
    .A0(A[4]), .B0(B[4]), .SELECT(SELECT_OPRATIONS), .OUTPUT(n1_bit_logical_1_output[3]));
  _2_BIT_BIDIRECTIONAL u_2_bit_bidirectional_1 (
    .I_P(I_P[1:0]), .I_P_BIT(I_P_BIT), .CONTROL(CONTROL), .O_P(n2_bit_bidirectional_1_o_p));
  Demultiplexer #(.width(2), .enable("false")) demultiplexer_1 (
    .out0(demultiplexer_1_out0), .out1(demultiplexer_1_out1), .in(n2_bit_bidirectional_1_o_p), .sel(CONTROL));
  _2_BIT_BIDIRECTIONAL u_2_bit_bidirectional_2 (
    .I_P(I_P[3:2]), .I_P_BIT(I_P_BIT), .CONTROL(CONTROL), .O_P(n2_bit_bidirectional_2_o_p));
  Demultiplexer #(.width(2), .enable("false")) demultiplexer_2 (
    .out0(demultiplexer_2_out0), .out1(demultiplexer_2_out1), .in(n2_bit_bidirectional_2_o_p), .sel(CONTROL));
  _1_BIT_ARITHMETIC u_1_bit_arithmetic_5 (
    .Cin(n1_bit_arithmetic_4_cout), .B0(B[2]), .A0(A[2]), .SELECT(SELECT_OPRATIONS),
    .S0(n1_bit_arithmetic_5_s0[0]), .Cout(n1_bit_arithmetic_5_cout));
  _1_BIT_LOGICAL u_1_bit_logical_5 (
    .A0(A[2]), .B0(B[2]), .SELECT(SELECT_OPRATIONS), .OUTPUT(n1_bit_logical_5_output[0]));
  _1_BIT_ARITHMETIC u_1_bit_arithmetic_6 (
    .Cin(n1_bit_arithmetic_5_cout), .B0(B[3]), .A0(A[3]), .SELECT(SELECT_OPRATIONS),
    .S0(n1_bit_arithmetic_5_s0[1]), .Cout(n1_bit_arithmetic_6_cout));
  _1_BIT_LOGICAL u_1_bit_logical_6 (
    .A0(A[3]), .B0(B[3]), .SELECT(SELECT_OPRATIONS), .OUTPUT(n1_bit_logical_5_output[1]));
  _1_BIT_ARITHMETIC u_1_bit_arithmetic_7 (
    .Cin(n1_bit_arithmetic_6_cout), .B0(B[1]), .A0(A[1]), .SELECT(SELECT_OPRATIONS),
    .S0(n1_bit_arithmetic_5_s0[2]), .Cout(n1_bit_arithmetic_7_cout));
  _1_BIT_LOGICAL u_1_bit_logical_7 (
    .A0(A[1]), .B0(B[1]), .SELECT(SELECT_OPRATIONS), .OUTPUT(n1_bit_logical_5_output[2]));
  _1_BIT_ARITHMETIC u_1_bit_arithmetic_8 (
    .Cin(n1_bit_arithmetic_7_cout), .B0(B[0]), .A0(A[0]), .SELECT(SELECT_OPRATIONS),
    .S0(n1_bit_arithmetic_5_s0[3]), .Cout(Cout));
  _1_BIT_LOGICAL u_1_bit_logical_8 (
    .A0(A[0]), .B0(B[0]), .SELECT(SELECT_OPRATIONS), .OUTPUT(n1_bit_logical_5_output[3]));
  Demultiplexer #(.width(2), .enable("false")) demultiplexer_3 (
    .out0(demultiplexer_3_out0), .out1(demultiplexer_3_out1), .in(n2_bit_bidirectional_3_o_p), .sel(CONTROL_2));
  _2_BIT_BIDIRECTIONAL u_2_bit_bidirectional_3 (
    .I_P(I_P[5:4]), .I_P_BIT(I_P_BIT_2), .CONTROL(CONTROL_2), .O_P(n2_bit_bidirectional_3_o_p));
  _2_BIT_BIDIRECTIONAL u_2_bit_bidirectional_4 (
    .I_P(I_P[7:6]), .I_P_BIT(I_P_BIT_2), .CONTROL(CONTROL_2), .O_P(n2_bit_bidirectional_4_o_p));
  Demultiplexer #(.width(2), .enable("false")) demultiplexer_4 (
    .out0(demultiplexer_4_out0), .out1(demultiplexer_4_out1), .in(n2_bit_bidirectional_4_o_p), .sel(CONTROL_2));
  Multiplexer #(.select(2), .width(4), .enable("false")) multiplexer_1 (
    .in0(n1_bit_arithmetic_1_s0), .in1(n1_bit_logical_1_output),
    .in2({demultiplexer_2_out0, demultiplexer_1_out0}), .in3({demultiplexer_2_out1, demultiplexer_1_out1}),
    .sel(ALU_SELECT_OPRATION));  // open: out
  Multiplexer #(.select(2), .width(4), .enable("false")) multiplexer_2 (
    .in0(n1_bit_arithmetic_5_s0), .in1(n1_bit_logical_5_output),
    .in2({demultiplexer_4_out0, demultiplexer_3_out0}), .in3({demultiplexer_4_out1, demultiplexer_3_out1}),
    .sel(ALU_SELECT_OPRATION));  // open: out

  // Notes on the sheet:
  //   0=> RIGHT SHEFT
  //   1=> LEFT SHEFT
  //   0=> RIGHT SHEFT
  //   1=> LEFT SHEFT
  //   23CS042
  //   23CS042
endmodule
