// Logisim project EXP 5.circ as structural Verilog
module _1_BIT_ARITHMATIC (
  input  CIN,
  input  A,
  input  B,
  input  [1:0] S1S0,
  output S,
  output COUT
);

  wire multiplexer_1_out, not_1_out;

  not not_1 (not_1_out, B);
  Multiplexer #(.select(2), .enable("false")) multiplexer_1 (
    .in0(B), .in1(not_1_out), .in2(1'b0), .in3(1'b1), .out(multiplexer_1_out), .sel(S1S0));
  Adder #(.width(1)) adder_1 (.a(A), .b(multiplexer_1_out), .out(S), .cin(CIN), .cout(COUT));

  // Notes on the sheet:
  //   1 BIT ARITHMATIC
  //   23CS042
endmodule

module _1_BIT_LOGICAL_CIRCUIT (
  input  BO,
  input  A0,
  input  [1:0] S1S0,
  output E0
);

  wire and_1_out, not_1_out, or_1_out, xor_1_out;

  and and_1 (and_1_out, A0, BO);
  or or_1 (or_1_out, A0, BO);
  xor xor_1 (xor_1_out, A0, BO);
  not not_1 (not_1_out, A0);
  Multiplexer #(.select(2), .enable("false")) multiplexer_1 (
    .in0(and_1_out), .in1(or_1_out), .in2(xor_1_out), .in3(not_1_out), .out(E0), .sel(S1S0));

  // Notes on the sheet:
  //   23CS042
  //   1  BIT LOGICAL
endmodule

module _8_BIT_ALU (
  input  [3:0] SELECT,
  input  SHL,
  input  SHR,
  input  [7:0] A,
  input  CIN,
  input  [7:0] B,
  output COUT,
  output [7:0] S1
);

  wire n1_bit_arithmatic_1_cout, n1_bit_arithmatic_1_s, n1_bit_arithmatic_2_cout, n1_bit_arithmatic_2_s,
       n1_bit_arithmatic_3_cout, n1_bit_arithmatic_3_s, n1_bit_arithmatic_4_cout, n1_bit_arithmatic_4_s,
       n1_bit_arithmatic_5_cout, n1_bit_arithmatic_5_s, n1_bit_arithmatic_6_cout, n1_bit_arithmatic_6_s,
       n1_bit_arithmatic_7_cout, n1_bit_arithmatic_7_s, n1_bit_arithmatic_8_s, n1_bit_logical_circuit_1_e0,
       n1_bit_logical_circuit_2_e0, n1_bit_logical_circuit_3_e0, n1_bit_logical_circuit_4_e0,
       n1_bit_logical_circuit_5_e0, n1_bit_logical_circuit_6_e0, n1_bit_logical_circuit_7_e0,
       n1_bit_logical_circuit_8_e0;

  _1_BIT_ARITHMATIC u_1_bit_arithmatic_1 (
    .A(A[0]), .B(B[0]), .S1S0(SELECT[1:0]), .CIN(CIN), .S(n1_bit_arithmatic_1_s),
    .COUT(n1_bit_arithmatic_1_cout));
  _1_BIT_LOGICAL_CIRCUIT u_1_bit_logical_circuit_1 (
    .S1S0(SELECT[1:0]), .BO(B[0]), .A0(A[0]), .E0(n1_bit_logical_circuit_1_e0));
  _1_BIT_ARITHMATIC u_1_bit_arithmatic_2 (
    .A(A[1]), .B(B[1]), .S1S0(SELECT[1:0]), .CIN(n1_bit_arithmatic_1_cout), .S(n1_bit_arithmatic_2_s),
    .COUT(n1_bit_arithmatic_2_cout));
  _1_BIT_LOGICAL_CIRCUIT u_1_bit_logical_circuit_2 (
    .S1S0(SELECT[1:0]), .BO(B[1]), .A0(A[1]), .E0(n1_bit_logical_circuit_2_e0));
  _1_BIT_ARITHMATIC u_1_bit_arithmatic_3 (
    .A(A[2]), .B(B[2]), .S1S0(SELECT[1:0]), .CIN(n1_bit_arithmatic_2_cout), .S(n1_bit_arithmatic_3_s),
    .COUT(n1_bit_arithmatic_3_cout));
  _1_BIT_LOGICAL_CIRCUIT u_1_bit_logical_circuit_3 (
    .S1S0(SELECT[1:0]), .BO(B[2]), .A0(A[2]), .E0(n1_bit_logical_circuit_3_e0));
  _1_BIT_ARITHMATIC u_1_bit_arithmatic_4 (
    .A(A[3]), .B(B[3]), .S1S0(SELECT[1:0]), .CIN(n1_bit_arithmatic_3_cout), .S(n1_bit_arithmatic_4_s),
    .COUT(n1_bit_arithmatic_4_cout));
  _1_BIT_LOGICAL_CIRCUIT u_1_bit_logical_circuit_4 (
    .S1S0(SELECT[1:0]), .BO(B[3]), .A0(A[3]), .E0(n1_bit_logical_circuit_4_e0));
  _1_BIT_ARITHMATIC u_1_bit_arithmatic_5 (
    .A(A[4]), .B(B[4]), .S1S0(SELECT[1:0]), .CIN(n1_bit_arithmatic_4_cout), .S(n1_bit_arithmatic_5_s),
    .COUT(n1_bit_arithmatic_5_cout));
  _1_BIT_LOGICAL_CIRCUIT u_1_bit_logical_circuit_5 (
    .S1S0(SELECT[1:0]), .BO(B[4]), .A0(A[4]), .E0(n1_bit_logical_circuit_5_e0));
  _1_BIT_ARITHMATIC u_1_bit_arithmatic_6 (
    .A(A[5]), .B(B[5]), .S1S0(SELECT[1:0]), .CIN(n1_bit_arithmatic_5_cout), .S(n1_bit_arithmatic_6_s),
    .COUT(n1_bit_arithmatic_6_cout));
  _1_BIT_LOGICAL_CIRCUIT u_1_bit_logical_circuit_6 (
    .S1S0(SELECT[1:0]), .BO(B[5]), .A0(A[5]), .E0(n1_bit_logical_circuit_6_e0));
  _1_BIT_ARITHMATIC u_1_bit_arithmatic_7 (
    .A(A[6]), .B(B[6]), .S1S0(SELECT[1:0]), .CIN(n1_bit_arithmatic_6_cout), .S(n1_bit_arithmatic_7_s),
    .COUT(n1_bit_arithmatic_7_cout));
  _1_BIT_LOGICAL_CIRCUIT u_1_bit_logical_circuit_7 (
    .S1S0(SELECT[1:0]), .BO(B[6]), .A0(A[6]), .E0(n1_bit_logical_circuit_7_e0));
  _1_BIT_ARITHMATIC u_1_bit_arithmatic_8 (
    .A(A[7]), .B(B[7]), .S1S0(SELECT[1:0]), .CIN(n1_bit_arithmatic_7_cout), .S(n1_bit_arithmatic_8_s),
    .COUT(COUT));
  _1_BIT_LOGICAL_CIRCUIT u_1_bit_logical_circuit_8 (
    .S1S0(SELECT[1:0]), .BO(B[7]), .A0(A[7]), .E0(n1_bit_logical_circuit_8_e0));
  Multiplexer #(.select(2), .enable("false")) multiplexer_1 (
    .in0(n1_bit_arithmatic_1_s), .in1(n1_bit_logical_circuit_1_e0), .in2(A[1]), .in3(SHL), .out(S1[0]),
    .sel(SELECT[3:2]));
  Multiplexer #(.select(2), .enable("false")) multiplexer_2 (
    .in0(n1_bit_arithmatic_2_s), .in1(n1_bit_logical_circuit_2_e0), .in2(A[2]), .in3(A[0]), .out(S1[1]),
    .sel(SELECT[3:2]));
  Multiplexer #(.select(2), .enable("false")) multiplexer_3 (
    .in0(n1_bit_arithmatic_3_s), .in1(n1_bit_logical_circuit_3_e0), .in2(A[3]), .in3(A[1]), .out(S1[2]),
    .sel(SELECT[3:2]));
  Multiplexer #(.select(2), .enable("false")) multiplexer_4 (
    .in0(n1_bit_arithmatic_4_s), .in1(n1_bit_logical_circuit_4_e0), .in2(A[4]), .in3(A[2]), .out(S1[3]),
    .sel(SELECT[3:2]));
  Multiplexer #(.select(2), .enable("false")) multiplexer_5 (
    .in0(n1_bit_arithmatic_5_s), .in1(n1_bit_logical_circuit_5_e0), .in2(A[5]), .in3(A[3]), .out(S1[4]),
    .sel(SELECT[3:2]));
  Multiplexer #(.select(2), .enable("false")) multiplexer_6 (
    .in0(n1_bit_arithmatic_6_s), .in1(n1_bit_logical_circuit_6_e0), .in2(A[6]), .in3(A[4]), .out(S1[5]),
    .sel(SELECT[3:2]));
  Multiplexer #(.select(2), .enable("false")) multiplexer_7 (
    .in0(n1_bit_arithmatic_7_s), .in1(n1_bit_logical_circuit_7_e0), .in2(A[7]), .in3(A[5]), .out(S1[6]),
    .sel(SELECT[3:2]));
  Multiplexer #(.select(2), .enable("false")) multiplexer_8 (
    .in0(n1_bit_arithmatic_8_s), .in1(n1_bit_logical_circuit_8_e0), .in2(SHR), .in3(A[6]), .out(S1[7]),
    .sel(SELECT[3:2]));

  // Notes on the sheet:
  //   B7B6B5B4B2B1B0
  //   8 BIT ALU
  //   A7A6A5A4A3A2A1A0
  //   S3S2S1S0
  //   23CS042
endmodule

module _16_BIT_ALU (
  input  [3:0] SELECT,
  input  SHL,
  input  [15:0] A,
  input  CIN,
  input  [15:0] B,
  input  SHR,
  output [15:0] OUTPUT,
  output Cout
);

  wire n8_bit_alu_1_cout;

  _8_BIT_ALU u_8_bit_alu_1 (
    .SELECT(SELECT), .A(A[7:0]), .CIN(CIN), .B(B[7:0]), .SHL(SHL), .SHR(A[7]), .S1(OUTPUT[7:0]),
    .COUT(n8_bit_alu_1_cout));
  _8_BIT_ALU u_8_bit_alu_2 (
    .SELECT(SELECT), .A(A[15:8]), .CIN(n8_bit_alu_1_cout), .B(B[15:8]), .SHL(A[8]), .SHR(SHR),
    .S1(OUTPUT[15:8]), .COUT(Cout));

  // Notes on the sheet:
  //   23CS042
  //   BIT 0 TO 7
  //   BIT 8 TO 15
endmodule

module commonbus (
  input  [11:0] ADDRESS,
  input  SELECT_A,
  input  [15:0] DATA,
  input  SELECT_D,
  input  [2:0] CONTROL_AR,
  input  CLR,
  input  WRITE,
  input  READ,
  input  SELECT_RAM,
  input  [2:0] CONTROL_PC,
  input  [2:0] CONTROL_DR,
  input  [3:0] SELECT_ALU,
  input  [2:0] CONTROL_AC,
  input  [2:0] CONTROL_CB,
  input  [1:0] SELECT_MUX_A,
  input  Cin,
  input  [2:0] SELECT,
  input  [1:0] SELECT_MUX_B,
  input  SHL,
  input  [2:0] CONTROL_IR,
  input  SHR,
  input  [2:0] CONTROL_TR,
  input  [7:0] INPR,
  input  [2:0] CONTROL_OUTR,
  output [15:0] CB_O_P,
  output E
);

  wire CB_CLK_out, clock_1_out, SYSTEM_CLK_out;
  wire [11:0] AR_q, multiplexer_1_out, PC_q;
  wire [15:0] AC_q, DR_q, IR_q, multiplexer_2_out, multiplexer_3_out, multiplexer_4_out, multiplexer_5_out,
       n16_bit_alu_1_output, ram_1_data, TR_q;

  Multiplexer #(.width(12), .enable("false")) multiplexer_1 (
    .in0(AR_q), .in1(ADDRESS), .out(multiplexer_1_out), .sel(SELECT_A));
  Multiplexer #(.width(16), .enable("false")) multiplexer_2 (
    .in0(CB_O_P), .in1(DATA), .out(multiplexer_2_out), .sel(SELECT_D));
  Clock clock_1 (.out(clock_1_out));
  Multiplexer #(.select(2), .width(16), .enable("false")) multiplexer_3 (
    .in0(DR_q), .in1({{8{1'b0}}, INPR}), .in2(AC_q), .out(multiplexer_3_out), .sel(SELECT_MUX_A));  // open: in3
  Multiplexer #(.select(2), .width(16), .enable("false")) multiplexer_4 (
    .in0(DR_q), .in1({{8{1'b0}}, INPR}), .in2(AC_q), .out(multiplexer_4_out), .sel(SELECT_MUX_B));  // open: in3
  RAM #(.addrWidth(12), .dataWidth(16), .bus("separate")) ram_1 (
    .addr(multiplexer_1_out), .din(multiplexer_2_out), .data(ram_1_data), .str(WRITE), .sel(SELECT_RAM),
    .clk(clock_1_out), .ld(READ), .clr(CLR));
  _16_BIT_ALU u_16_bit_alu_1 (
    .SELECT(SELECT_ALU), .SHL(SHL), .A(multiplexer_3_out), .CIN(Cin), .B(multiplexer_4_out), .SHR(SHR),
    .OUTPUT(n16_bit_alu_1_output), .Cout(E));
  Counter #(.width(12), .max('hfff)) AR (
    .load(CONTROL_AR[0]), .D(CB_O_P[11:0]), .count(CONTROL_AR[1]), .Q(AR_q), .clk(SYSTEM_CLK_out),
    .clr(CONTROL_AR[2]));  // open: carry
  Counter #(.width(12), .max('hfff)) PC (
    .load(CONTROL_PC[0]), .D(CB_O_P[11:0]), .count(CONTROL_PC[1]), .Q(PC_q), .clk(SYSTEM_CLK_out),
    .clr(CONTROL_PC[2]));  // open: carry
  Counter #(.width(16), .max('hffff)) DR (
    .load(CONTROL_DR[0]), .D(CB_O_P), .count(CONTROL_DR[1]), .Q(DR_q), .clk(SYSTEM_CLK_out),
    .clr(CONTROL_DR[2]));  // open: carry
  Counter #(.width(16), .max('hffff)) AC (
    .load(CONTROL_AC[0]), .D(n16_bit_alu_1_output), .count(CONTROL_AC[1]), .Q(AC_q), .clk(SYSTEM_CLK_out),
    .clr(CONTROL_AC[2]));  // open: carry
  Register #(.width(16)) IR (.D(CB_O_P), .en(CONTROL_IR[0]), .Q(IR_q), .clk(SYSTEM_CLK_out), .clr(CONTROL_IR[2]));
  Counter #(.width(16), .max('hffff)) TR (
    .load(CONTROL_TR[0]), .D(CB_O_P), .count(CONTROL_TR[1]), .Q(TR_q), .clk(SYSTEM_CLK_out),
    .clr(CONTROL_TR[2]));  // open: carry
  Register OUTR (.D(CB_O_P[7:0]), .en(CONTROL_OUTR[0]), .clk(SYSTEM_CLK_out), .clr(CONTROL_OUTR[2]));  // open: Q
  Clock SYSTEM_CLK (.out(SYSTEM_CLK_out));
  Multiplexer #(.select(3), .width(16), .enable("false")) multiplexer_5 (
    .in1({4'b0000, AR_q}), .in2({4'b0000, PC_q}), .in3(DR_q), .in4(AC_q), .in5(IR_q), .in6(TR_q),
    .in7(ram_1_data), .out(multiplexer_5_out), .sel(SELECT));  // open: in0
  Register #(.width(16)) register_1 (
    .D(multiplexer_5_out), .en(CONTROL_CB[0]), .Q(CB_O_P), .clk(CB_CLK_out), .clr(CONTROL_CB[2]));
  Clock CB_CLK (.out(CB_CLK_out));

  // Notes on the sheet:
  //   CONTROL 
  //   BIT 0=>LOAD
  //   BIT 1=>INR
  //   BIT 2=>CLEAR
endmodule
